// Digital circuit mainBus.dig as structural Verilog
module mainBus (
  input  clk,
  input  [7:0] in_2
);

  wire dipswitch_1_out, dipswitch_2_out, dipswitch_3_out, dipswitch_4_out;
  wire [3:0] Reg_A_q_x, Reg_A_q_x_2;
  wire [4:0] Reg_I_p3;
  wire [7:0] Reg_I_2_q_x;
  wire [11:0] ID_out;

  DipSwitch dipswitch_1 (.out(dipswitch_1_out));
  DipSwitch dipswitch_2 (.out(dipswitch_2_out));
  DipSwitch dipswitch_3 (.out(dipswitch_3_out));
  DipSwitch dipswitch_4 (.out(dipswitch_4_out));
  _5bitPC2 _5bitpc2_1 (
    .PC_in(in_2), .Le_a(dipswitch_1_out), .CNTe_a(dipswitch_2_out), .CLK(clk), .CLR(dipswitch_3_out),
    .Re_a(dipswitch_4_out));  // open: PC_out
  sapRegX Reg_A (.D_x({Reg_A_q_x_2, Reg_A_q_x}), .Q_x({Reg_A_q_x_2, Reg_A_q_x}));  // open: E_in, E_out
  sapRegX Reg_C (.D_x({Reg_A_q_x_2, Reg_A_q_x}), .Q_x({Reg_A_q_x_2, Reg_A_q_x}));  // open: E_in, E_out
  // sapRegX Reg_I: pin names not known; wires that end beside it: 1'b1, {Reg_A_q_x_2, Reg_A_q_x}, Reg_I_p3, {Reg_A_q_x_2, Reg_A_q_x}
  ROM #(.AddrBits(5), .Bits(13)) PGM_mem (.A(Reg_I_p3), .sel(1'b1));  // open: D
  LookUpTable #(.Bits(12)) ID (.out(ID_out));  // open: in0, in1, in2, in3
  Seven_Seg_Hex seven_seg_hex_1 (.d(Reg_A_q_x_2), .dp(1'b0));
  sapRegX Reg_B (.D_x({Reg_A_q_x_2, Reg_A_q_x}), .Q_x({Reg_A_q_x_2, Reg_A_q_x}));  // open: E_in, E_out
  // sapRegX Reg_W: pin names not known; wires that end beside it: {Reg_A_q_x_2, Reg_A_q_x}
  sapRegX Reg_I_2 (.D_x({Reg_A_q_x_2, Reg_A_q_x}), .E_out(1'b1), .Q_x(Reg_I_2_q_x));  // open: E_in
  Seven_Seg_Hex seven_seg_hex_2 (.d(Reg_A_q_x), .dp(1'b0));
  RAMDualPort #(.AddrBits(8), .Bits(8)) RAM (
    .A(Reg_I_2_q_x), .Din({Reg_A_q_x_2, Reg_A_q_x}), .D({Reg_A_q_x_2, Reg_A_q_x}));  // open: str, C, ld

  // Notes on the sheet:
  //   in_2: default 5
  //   Formato da instrução
  //   OOOOAAAAAAAA
  //   OOOO -> Codigo de instrucao
  //   AAAAAAAA -->> Endereco do operando / valor
  //   256 byte
  //   ScratchPad memory
endmodule
